# Fritzing sketch AND (saved by Fritzing 0.8.0b)
breadboards: 1

parts:
  S1 = Pushbutton [package="[THT]"]
  S2 = Pushbutton [package="[THT]"]
  R1 = Resistor [tolerance=±5% resistance=330 package=THT]
  R2 = Resistor [tolerance=±5% resistance=330 package=THT]
  LED1 = LED - 5mm [color="Blue (505nm)" package="5 mm [THT]"]
  U1 = Voltage Regulator - 5V [package="TO220 [THT]"]
  R3 = Resistor [tolerance=±5% resistance=220 package=THT]
  PIC16F886 = IC, DIP package, 28 pins [chip_label=PIC16F886]
  VCC1 = Battery block 9V

nets:
  N1: S1.Pin_1, S1.Pin_2, R2.Pin_1, PIC16F886.pin3
  N2: S1.Pin_3, S1.Pin_4, S2.Pin_3, S2.Pin_4, U1.output_voltage, PIC16F886.pin20
  N3: S2.Pin_1, S2.Pin_2, R1.Pin_1, PIC16F886.pin2
  GND: R1.Pin_0, R2.Pin_0, U1.GND, R3.Pin_0, PIC16F886.pin8, PIC16F886.pin19, VCC1.-
  N4: LED1.cathode, R3.Pin_1
  N5: LED1.anode, PIC16F886.pin21
  N6: U1.input_voltage, VCC1.+
