# Fritzing sketch Hola Mundo (saved by Fritzing 0.8.0b)
breadboards: 1

parts:
  LED1 = LED - 5mm [color="Red (633nm)" package="5 mm [THT]"]
  U1 = Voltage Regulator - 5V [package="TO220 [THT]"]
  VCC1 = Battery block 9V
  R2 = Resistor [tolerance=±5% resistance=220 package=THT]
  PIC16F886 = IC, DIP package, 28 pins [chip_label=PIC16F886]

nets:
  N1: LED1.cathode, R2.Pin_1
  N2: LED1.anode, PIC16F886.pin21
  N3: U1.input_voltage, VCC1.+
  GND: U1.GND, VCC1.-, R2.Pin_0, PIC16F886.pin8, PIC16F886.pin19
  N4: U1.output_voltage, PIC16F886.pin20
