# Fritzing sketch HolaMundoEnsamblador (saved by Fritzing 0.8.0b)
breadboards: 1

parts:
  IC1 = IC, DIP package, 28 pins [chip_label=PIC16F886]
  LED1 = LED - 5mm [color="Red (633nm)" package="5 mm [THT]"]
  U1 = Voltage Regulator - 5V [package="TO220 [THT]"]
  VCC1 = Battery block 9V
  R1 = Resistor [package="0402 [SMD]"]  # not connected
  R2 = Resistor [tolerance=±5% resistance=220 package=THT]

nets:
  N1: IC1.pin8, IC1.pin19, U1.GND, VCC1.-, R2.Pin_0
  N2: IC1.pin20, U1.output_voltage
  N3: IC1.pin21, LED1.anode
  N4: LED1.cathode, R2.Pin_1
  N5: U1.input_voltage, VCC1.+
